// Logisim project alu_control.circ as structural Verilog: 1 circuit, main circuit main
module main (
  input  [1:0] ALU_Op,
  input  [2:0] Func3,
  input  [6:0] Func7,
  output [3:0] ALU_Signal
);

  wire _00, _000, _0000000, _001, _01, _010, _10, _011, _100, _101, _110, _111, _0100000, and_2_out,
       and_3_out, and_4_out, and_5_out, and_6_out, and_7_out, and_8_out, and_9_out, and_10_out, and_11_out,
       and_12_out, or_2_out, SRA, SUB;

  Comparator #(.width(2)) comparator_1 (.a(ALU_Op), .b(2'b00), .eq(_00));  // open: gt, lt
  Comparator #(.width(2)) comparator_2 (.a(ALU_Op), .b(2'b01), .eq(_01));  // open: gt, lt
  Comparator #(.width(2)) comparator_3 (.a(ALU_Op), .b(2'b10), .eq(_10));  // open: gt, lt
  Comparator #(.width(7)) comparator_4 (.a(Func7), .b({7{1'b0}}), .eq(_0000000));  // open: gt, lt
  Comparator #(.width(7)) comparator_5 (.a(Func7), .b(7'b0100000), .eq(_0100000));  // open: gt, lt
  and and_1 (SRA, _0100000, _10, _101);
  Comparator #(.width(3)) comparator_6 (.a(Func3), .b(3'b000), .eq(_000));  // open: gt, lt
  Comparator #(.width(3)) comparator_7 (.a(Func3), .b(3'b001), .eq(_001));  // open: gt, lt
  Comparator #(.width(3)) comparator_8 (.a(Func3), .b(3'b010), .eq(_010));  // open: gt, lt
  Comparator #(.width(3)) comparator_9 (.a(Func3), .b(3'b011), .eq(_011));  // open: gt, lt
  Comparator #(.width(3)) comparator_10 (.a(Func3), .b(3'b100), .eq(_100));  // open: gt, lt
  Comparator #(.width(3)) comparator_11 (.a(Func3), .b(3'b101), .eq(_101));  // open: gt, lt
  Comparator #(.width(3)) comparator_12 (.a(Func3), .b(3'b110), .eq(_110));  // open: gt, lt
  Comparator #(.width(3)) comparator_13 (.a(Func3), .b(3'b111), .eq(_111));  // open: gt, lt
  and and_2 (and_2_out, _0100000, _000, _10);
  or or_1 (SUB, and_2_out, _01);
  and and_3 (and_3_out, _0000000, _10);
  and and_4 (and_4_out, _0000000, _10);
  and and_5 (and_5_out, _10, _0000000, _011);
  and and_6 (and_6_out, _111, and_3_out);
  and and_7 (and_7_out, _110, and_3_out);
  and and_8 (and_8_out, _000, and_4_out);
  or or_2 (or_2_out, _00, and_8_out);
  and and_9 (and_9_out, and_3_out, _010);
  and and_10 (and_10_out, and_3_out, _100);
  and and_11 (and_11_out, and_3_out, _101);
  and and_12 (and_12_out, and_3_out, _001);
  Priority_Encoder #(.select(4)) priority_encoder_1 (
    .in0(and_6_out), .in1(and_7_out), .in2(or_2_out), .in3(and_5_out), .in6(SUB), .in7(and_9_out),
    .in8(and_10_out), .in10(SRA), .in14(and_11_out), .in15(and_12_out), .out(ALU_Signal));  // open: in4, in5, in9, in11, in12, in13, gs, en_out, en_in

  // Notes on the sheet:
  //   Added SLTU (Not in Tutorials)
endmodule
