// Logisim project cache_unit(notused).circ as structural Verilog: 1 circuit, main circuit main
module main (
  input  [31:0] Address,
  input  [31:0] Data,
  input  in_3,
  input  in_4,
  output Hit,
  output [31:0] Data_output
);

  wire and_1_out, clock_1_out, clock_2_out, comparator_1_eq, not_1_out, valid;
  wire [26:0] ram_1_data;
  wire [31:0] bit_extender_1_out, bit_extender_2_out, bit_extender_3_out, ram_2_data;

  Clock clock_1 (.out(clock_1_out));
  not not_1 (not_1_out, comparator_1_eq);
  and and_1 (and_1_out, in_3, valid);
  Clock clock_2 (.out(clock_2_out));
  RAM #(.addrWidth(3), .dataWidth(28), .bus("separate")) ram_1 (
    .addr(Address[4:2]), .din({1'b1, Address[31:5]}), .data({valid, ram_1_data}), .str(not_1_out),
    .clk(clock_1_out), .ld(1'b1));  // open: sel, clr
  RAM #(.addrWidth(3), .dataWidth(32), .bus("separate")) ram_2 (
    .addr(Address[4:2]), .din(Data), .data(ram_2_data), .str(and_1_out), .clk(clock_2_out), .ld(in_4));  // open: sel, clr
  Comparator #(.width(27)) comparator_1 (.a(ram_1_data), .b(Address[31:5]), .eq(comparator_1_eq));  // open: gt, lt
  assign bit_extender_1_out = {{8{1'b0}}, ram_2_data[31:8]};  // Bit_Extender bit_extender_1
  assign bit_extender_2_out = {{16{1'b0}}, ram_2_data[31:16]};  // Bit_Extender bit_extender_2
  assign bit_extender_3_out = {{24{1'b0}}, ram_2_data[31:24]};  // Bit_Extender bit_extender_3
  and and_2 (Hit, comparator_1_eq, valid);
  Multiplexer #(.select(2), .width(32)) multiplexer_1 (
    .in0(ram_2_data), .in1(bit_extender_1_out), .in2(bit_extender_2_out), .in3(bit_extender_3_out),
    .out(Data_output), .sel(Address[1:0]));  // open: en

  // Other names for the same wires on the sheet: tag[26:0] = Address[31:5]; offset[1:0] = Address[1:0];
  //   index[2:0] = Address[4:2]; Data_input[31:0] = Data; ldr = in_4; str = in_3
endmodule
