// Logisim project hazard_unit(notused).circ as structural Verilog: 1 circuit, main circuit main
module main (
  input  [4:0] rs1,
  input  [4:0] rs2,
  input  [4:0] EXRd,
  input  [4:0] MEMRd,
  input  EXWE,
  input  EXLoad,
  input  Rs2_Used,
  input  MEMWE,
  input  ID_B,
  output [1:0] Rs1Mux,
  output [1:0] Rs2Mux,
  output [1:0] RBMux,
  output Stall
);

  wire and_1_out, and_3_out, and_4_out, and_5_out, and_7_out, and_10_out, and_11_out, and_12_out, and_13_out,
       comparator_1_lt, comparator_4_lt, comparator_5_eq, comparator_6_eq, comparator_7_eq, comparator_8_eq,
       comparator_9_eq, comparator_10_eq, comparator_11_eq, comparator_12_eq, comparator_13_eq,
       comparator_14_eq, EXOut, EXRs1, EXRs2, MemOut, MemRs1, MemRs2, nand_1_out, nand_2_out, nand_3_out,
       not_1_out, not_2_out, not_3_out, not_4_out, not_5_out, not_6_out, not_7_out, not_8_out, or_1_out,
       or_2_out, or_3_out;

  Comparator #(.width(5)) comparator_1 (.a(EXRd), .b({5{1'b0}}), .lt(comparator_1_lt));  // open: gt, eq
  Comparator #(.width(5)) comparator_2 (.a(rs1), .b(EXRd), .eq(EXRs1));  // open: gt, lt
  Comparator #(.width(5)) comparator_3 (.a(rs2), .b(EXRd), .eq(EXRs2));  // open: gt, lt
  Comparator #(.width(5)) comparator_4 (.a(MEMRd), .b({5{1'b0}}), .lt(comparator_4_lt));  // open: gt, eq
  Comparator #(.width(1)) comparator_5 (.a(MEMWE), .b(1'b0), .eq(comparator_5_eq));  // open: gt, lt
  Comparator #(.width(5)) comparator_6 (.a(rs1), .b(MEMRd), .eq(comparator_6_eq));  // open: gt, lt
  Comparator #(.width(5)) comparator_7 (.a(rs2), .b(MEMRd), .eq(comparator_7_eq));  // open: gt, lt
  not not_1 (not_1_out, comparator_1_lt);
  and and_1 (and_1_out, not_1_out, EXWE);
  or or_1 (or_1_out, EXRs1, EXRs2);
  not not_2 (not_2_out, comparator_4_lt);
  and and_2 (MemOut, not_2_out, not_3_out);
  not not_3 (not_3_out, comparator_5_eq);
  not not_4 (not_4_out, EXOut);
  and and_3 (and_3_out, comparator_7_eq, not_5_out);
  not not_5 (not_5_out, EXOut);
  and and_4 (and_4_out, EXRs1, and_1_out);
  and and_5 (and_5_out, EXRs2, and_1_out);
  and and_6 (EXOut, and_1_out, or_1_out);
  and and_7 (and_7_out, comparator_6_eq, not_4_out);
  and and_8 (MemRs2, MemOut, and_3_out);
  and and_9 (MemRs1, MemOut, and_7_out);
  nand nand_1 (nand_1_out, and_5_out, MemRs2);
  nand nand_2 (nand_2_out, and_4_out, MemRs1);
  Priority_Encoder #(.select(2)) priority_encoder_1 (
    .in0(nand_2_out), .in1(and_4_out), .in2(MemRs1), .out(Rs1Mux));  // open: in3, gs, en_out, en_in
  Priority_Encoder #(.select(2)) priority_encoder_2 (
    .in0(nand_1_out), .in1(and_5_out), .in2(MemRs2), .out(Rs2Mux));  // open: in3, gs, en_out, en_in
  not not_6 (not_6_out, comparator_8_eq);
  Comparator #(.width(5)) comparator_8 (.a(EXRd), .b({5{1'b0}}), .eq(comparator_8_eq));  // open: gt, lt
  Comparator #(.width(5)) comparator_9 (.a(EXRd), .b(rs2), .eq(comparator_9_eq));  // open: gt, lt
  Comparator #(.width(5)) comparator_10 (.a(MEMRd), .b({5{1'b0}}), .eq(comparator_10_eq));  // open: gt, lt
  Comparator #(.width(5)) comparator_11 (.a(MEMRd), .b(rs2), .eq(comparator_11_eq));  // open: gt, lt
  and and_10 (and_10_out, EXWE, ID_B);
  Comparator #(.width(5)) comparator_12 (.a(EXRd), .b({5{1'b0}}), .eq(comparator_12_eq));  // open: gt, lt
  Comparator #(.width(5)) comparator_13 (.a(rs1), .b(EXRd), .eq(comparator_13_eq));  // open: gt, lt
  Comparator #(.width(5)) comparator_14 (.a(rs2), .b(EXRd), .eq(comparator_14_eq));  // open: gt, lt
  not not_7 (not_7_out, comparator_10_eq);
  or or_2 (or_2_out, EXLoad, and_10_out);
  not not_8 (not_8_out, comparator_12_eq);
  and and_11 (and_11_out, comparator_14_eq, Rs2_Used);
  and and_12 (and_12_out, not_6_out, comparator_9_eq, EXWE);
  or or_3 (or_3_out, comparator_13_eq, and_11_out);
  nand nand_3 (nand_3_out, and_12_out, and_13_out);
  and and_13 (and_13_out, not_7_out, comparator_11_eq, MEMWE, ~and_12_out);  // AND_Gate
  and and_14 (Stall, or_2_out, not_8_out, or_3_out);
  Priority_Encoder #(.select(2)) priority_encoder_3 (
    .in0(nand_3_out), .in1(and_12_out), .in2(and_13_out), .out(RBMux));  // open: in3, gs, en_out, en_in
endmodule
