// Logisim project main_control.circ as structural Verilog: 1 circuit, main circuit main
module main (
  input  [6:0] OP_CODE,
  output [1:0] ImmSRC,
  output Jump,
  output [1:0] ALU_Op,
  output Branch,
  output MemToReg,
  output Load,
  output Store,
  output AluSRC,
  output Write,
  output Rs2_Used
);

  wire comparator_1_eq, comparator_2_eq, comparator_3_eq, comparator_4_eq, comparator_5_eq, comparator_6_eq,
       comparator_7_eq, comparator_8_eq, comparator_9_eq;
  wire [3:0] multiplexer_1_out, multiplexer_2_out, multiplexer_3_out, multiplexer_4_out, multiplexer_5_out,
       multiplexer_6_out, multiplexer_7_out, multiplexer_8_out, multiplexer_9_out, or_1_out, or_2_out;
  wire [10:1] multiplexer_11_out;

  Comparator #(.width(7)) comparator_1 (.a(OP_CODE), .b(7'b0110011), .eq(comparator_1_eq));  // open: gt, lt
  Comparator #(.width(7)) comparator_2 (.a(OP_CODE), .b(7'b0010011), .eq(comparator_2_eq));  // open: gt, lt
  Comparator #(.width(7)) comparator_3 (.a(OP_CODE), .b(7'b0000011), .eq(comparator_3_eq));  // open: gt, lt
  Comparator #(.width(7)) comparator_4 (.a(OP_CODE), .b(7'b0100011), .eq(comparator_4_eq));  // open: gt, lt
  Comparator #(.width(7)) comparator_5 (.a(OP_CODE), .b(7'b1100111), .eq(comparator_5_eq));  // open: gt, lt
  Comparator #(.width(7)) comparator_6 (.a(OP_CODE), .b(7'b1100011), .eq(comparator_6_eq));  // open: gt, lt
  Comparator #(.width(7)) comparator_7 (.a(OP_CODE), .b(7'b0110111), .eq(comparator_7_eq));  // open: gt, lt
  Comparator #(.width(7)) comparator_8 (.a(OP_CODE), .b(7'b0010111), .eq(comparator_8_eq));  // open: gt, lt
  Comparator #(.width(7)) comparator_9 (.a(OP_CODE), .b(7'b1101111), .eq(comparator_9_eq));  // open: gt, lt
  Multiplexer #(.width(4)) multiplexer_1 (
    .in0(4'b0000), .in1(4'b0001), .out(multiplexer_1_out), .sel(comparator_1_eq));  // open: en
  Multiplexer #(.width(4)) multiplexer_2 (
    .in0(4'b0000), .in1(4'b0010), .out(multiplexer_2_out), .sel(comparator_2_eq));  // open: en
  Multiplexer #(.width(4)) multiplexer_3 (
    .in0(4'b0000), .in1(4'b0011), .out(multiplexer_3_out), .sel(comparator_3_eq));  // open: en
  Multiplexer #(.width(4)) multiplexer_4 (
    .in0(4'b0000), .in1(4'b0100), .out(multiplexer_4_out), .sel(comparator_4_eq));  // open: en
  Multiplexer #(.width(4)) multiplexer_5 (
    .in0(4'b0000), .in1(4'b0101), .out(multiplexer_5_out), .sel(comparator_5_eq));  // open: en
  Multiplexer #(.width(4)) multiplexer_6 (
    .in0(4'b0000), .in1(4'b0110), .out(multiplexer_6_out), .sel(comparator_6_eq));  // open: en
  Multiplexer #(.width(4)) multiplexer_7 (
    .in0(4'b0000), .in1(4'b0111), .out(multiplexer_7_out), .sel(comparator_7_eq));  // open: en
  Multiplexer #(.width(4)) multiplexer_8 (
    .in0(4'b0000), .in1(4'b1000), .out(multiplexer_8_out), .sel(comparator_8_eq));  // open: en
  Multiplexer #(.width(4)) multiplexer_9 (
    .in0(4'b0000), .in1(4'b1001), .out(multiplexer_9_out), .sel(comparator_9_eq));  // open: en
  Multiplexer #(.select(4), .width(11)) multiplexer_10 (
    .in1(11'h410), .in2(11'h610), .in3(11'h6c0), .in4(11'h301), .in5(11'h604), .in6(11'haa), .in7(11'h603),
    .in8(11'h603), .in9(11'h607), .out({Write, AluSRC, Store, Load, MemToReg, Branch, ALU_Op, Jump, ImmSRC}),
    .sel(or_1_out));  // open: in0, in10, in11, in12, in13, in14, in15, en
  assign or_1_out = multiplexer_1_out | multiplexer_2_out | multiplexer_3_out | multiplexer_4_out | multiplexer_5_out | multiplexer_6_out | multiplexer_7_out | multiplexer_8_out | multiplexer_9_out;  // OR_Gate or_1, 4 bits wide
  assign or_2_out = multiplexer_1_out | multiplexer_4_out | multiplexer_6_out;  // OR_Gate or_2, 4 bits wide
  Multiplexer #(.select(4), .width(11)) multiplexer_11 (
    .in0(11'h1), .in1({11{1'b0}}), .in2({11{1'b0}}), .in3(11'h1), .in4({11{1'b0}}), .in5(11'h1),
    .in6({11{1'b0}}), .in7({11{1'b0}}), .in8({11{1'b0}}), .in9({11{1'b0}}), .in10({11{1'b0}}),
    .in11({11{1'b0}}), .in12({11{1'b0}}), .in13({11{1'b0}}), .in14({11{1'b0}}), .in15({11{1'b0}}),
    .out({multiplexer_11_out, Rs2_Used}), .sel(or_2_out));  // open: en

  // Notes on the sheet:
  //   I-Type
  //   B-Type
  //   R-Type
  //   I-Type (Load)
  //   S-Type
  //   I-Type (Jump)
  //   U-Type (LUI)
  //   U-Type (AUIPC)
  //   J-Type
  //   I-Type
  //   S-Type
  //   B-Type
  //   I-Type (Load)
  //   I-Type (Jump)
  //   U-Type (LUI)
  //   U-Type (AUIPC)
  //   R-Type
  //   J-Type
endmodule
