// Logisim project immediate_generator.circ as structural Verilog: 1 circuit, main circuit main
module main (
  input  [4:0] rd,
  input  [4:0] rs1,
  input  [4:0] rs2,
  input  [6:0] func7,
  input  [2:0] func3,
  input  [6:0] opcode,
  output [31:0] out_7
);

  wire and_1_out, comparator_1_eq, comparator_2_eq, comparator_3_eq, comparator_4_eq, comparator_5_eq,
       comparator_6_eq, comparator_7_eq, comparator_8_eq, comparator_9_eq, comparator_10_eq, i_star, or_2_out;
  wire [2:0] priority_encoder_1_out;
  wire [31:0] bit_extender_1_out, bit_extender_2_out, bit_extender_3_out, bit_extender_4_out,
       bit_extender_5_out, bit_extender_6_out;

  Comparator #(.width(3)) comparator_1 (.a(func3), .b(3'b101), .eq(comparator_1_eq));  // open: gt, lt
  Comparator #(.width(3)) comparator_2 (.a(func3), .b(3'b001), .eq(comparator_2_eq));  // open: gt, lt
  assign bit_extender_1_out = {{27{1'b0}}, rs2};  // Bit_Extender bit_extender_1
  assign bit_extender_2_out = {{20{func7[6]}}, {func7, rs2}};  // Bit_Extender bit_extender_2
  assign bit_extender_3_out = {{20{func7[6]}}, {func7, rs2}};  // Bit_Extender bit_extender_3
  assign bit_extender_4_out = {{20{func7[6]}}, {func7, rd}};  // Bit_Extender bit_extender_4
  assign bit_extender_5_out = {{19{func7[6]}}, {func7[6], rd[0], func7[5:0], rd[4:1], 1'b0}};  // Bit_Extender bit_extender_5
  assign bit_extender_6_out = {{11{func7[6]}}, {func7[6], rs1, func3, rs2[0], func7[5:0], rs2[4:1], 1'b0}};  // Bit_Extender bit_extender_6
  or or_1 (i_star, comparator_1_eq, comparator_2_eq);
  Comparator #(.width(7)) comparator_3 (.a(opcode), .b(7'b0010011), .eq(comparator_3_eq));  // open: gt, lt
  Comparator #(.width(7)) comparator_4 (.a(opcode), .b(7'b0000011), .eq(comparator_4_eq));  // open: gt, lt
  Comparator #(.width(7)) comparator_5 (.a(opcode), .b(7'b0100011), .eq(comparator_5_eq));  // open: gt, lt
  Comparator #(.width(7)) comparator_6 (.a(opcode), .b(7'b0010111), .eq(comparator_6_eq));  // open: gt, lt
  Comparator #(.width(7)) comparator_7 (.a(opcode), .b(7'b0110111), .eq(comparator_7_eq));  // open: gt, lt
  Comparator #(.width(7)) comparator_8 (.a(opcode), .b(7'b1100011), .eq(comparator_8_eq));  // open: gt, lt
  Comparator #(.width(7)) comparator_9 (.a(opcode), .b(7'b1101111), .eq(comparator_9_eq));  // open: gt, lt
  Comparator #(.width(7)) comparator_10 (.a(opcode), .b(7'b1100111), .eq(comparator_10_eq));  // open: gt, lt
  and and_1 (and_1_out, comparator_3_eq, i_star);
  or or_2 (or_2_out, comparator_3_eq, comparator_10_eq);
  Multiplexer #(.select(3), .width(32)) multiplexer_1 (
    .in0(bit_extender_1_out), .in1(bit_extender_2_out), .in2(bit_extender_3_out), .in3(bit_extender_4_out),
    .in4({func7, rs2, rs1, func3, {12{1'b0}}}), .in5({func7, rs2, rs1, func3, {12{1'b0}}}),
    .in6(bit_extender_5_out), .in7(bit_extender_6_out), .out(out_7), .sel(priority_encoder_1_out));  // open: en
  Priority_Encoder priority_encoder_1 (
    .in0(and_1_out), .in1(or_2_out), .in2(comparator_4_eq), .in3(comparator_5_eq), .in4(comparator_6_eq),
    .in5(comparator_7_eq), .in6(comparator_8_eq), .in7(comparator_9_eq), .out(priority_encoder_1_out));  // open: en_in, gs, en_out

  // Notes on the sheet:
  //   Decides whether it's I-type or I*-type
  //   I* Type
  //   I-Type
  //   Load
  //   S-Type
  //   Both U-Type
  //   B-Type
  //   J-Type
  //   I/I* type
  //   Load Immediate
  //   S-Type
  //   Both U-Type
  //   B-Type
  //   J-Type
  //   JALR
endmodule
