// Logisim project cpu_single_cycle.circ as structural Verilog: 4 circuits, main circuit Main
module Register_File (
  input  [31:0] Data,
  input  [31:0] X0,
  input  [4:0] RA,
  input  [4:0] RW,
  input  W,
  input  [4:0] RB,
  output [31:0] RA_Output,
  output [31:0] RB_Output
);

  wire and_1_out, and_2_out, and_3_out, and_4_out, and_5_out, and_6_out, and_7_out, and_8_out, and_9_out,
       and_10_out, and_11_out, and_12_out, and_13_out, and_14_out, and_15_out, and_16_out, and_17_out,
       and_18_out, and_19_out, and_20_out, and_21_out, and_22_out, and_23_out, and_24_out, and_25_out,
       and_26_out, and_27_out, and_28_out, and_29_out, and_30_out, and_31_out, and_32_out, clock_1_out,
       decoder_1_out0, decoder_1_out1, decoder_1_out2, decoder_1_out3, decoder_1_out4, decoder_1_out5,
       decoder_1_out6, decoder_1_out7, decoder_1_out8, decoder_1_out9, decoder_1_out10, decoder_1_out11,
       decoder_1_out12, decoder_1_out13, decoder_1_out14, decoder_1_out15, decoder_1_out16, decoder_1_out17,
       decoder_1_out18, decoder_1_out19, decoder_1_out20, decoder_1_out21, decoder_1_out22, decoder_1_out23,
       decoder_1_out24, decoder_1_out25, decoder_1_out26, decoder_1_out27, decoder_1_out28, decoder_1_out29,
       decoder_1_out30, decoder_1_out31;
  wire [31:0] x0_q, x1_q, x2_q, x3_q, x4_q, x5_q, x6_q, x7_q, x8_q, x9_q, x10_q, x11_q, x12_q, x13_q, x14_q,
       x15_q, x16_q, x17_q, x18_q, x19_q, x20_q, x21_q, x22_q, x23_q, x24_q, x25_q, x26_q, x27_q, x28_q,
       x29_q, x30_q, x31_q;

  Decoder #(.select(5)) decoder_1 (
    .out0(decoder_1_out0), .out1(decoder_1_out1), .out2(decoder_1_out2), .out3(decoder_1_out3),
    .out4(decoder_1_out4), .out5(decoder_1_out5), .out6(decoder_1_out6), .out7(decoder_1_out7),
    .out8(decoder_1_out8), .out9(decoder_1_out9), .out10(decoder_1_out10), .out11(decoder_1_out11),
    .out12(decoder_1_out12), .out13(decoder_1_out13), .out14(decoder_1_out14), .out15(decoder_1_out15),
    .out16(decoder_1_out16), .out17(decoder_1_out17), .out18(decoder_1_out18), .out19(decoder_1_out19),
    .out20(decoder_1_out20), .out21(decoder_1_out21), .out22(decoder_1_out22), .out23(decoder_1_out23),
    .out24(decoder_1_out24), .out25(decoder_1_out25), .out26(decoder_1_out26), .out27(decoder_1_out27),
    .out28(decoder_1_out28), .out29(decoder_1_out29), .out30(decoder_1_out30), .out31(decoder_1_out31),
    .sel(RW));  // open: en
  Clock clock_1 (.out(clock_1_out));
  and and_1 (and_1_out, decoder_1_out0, W);
  and and_2 (and_2_out, decoder_1_out1, W);
  and and_3 (and_3_out, decoder_1_out2, W);
  and and_4 (and_4_out, decoder_1_out3, W);
  and and_5 (and_5_out, decoder_1_out4, W);
  and and_6 (and_6_out, decoder_1_out5, W);
  and and_7 (and_7_out, decoder_1_out6, W);
  and and_8 (and_8_out, decoder_1_out7, W);
  and and_9 (and_9_out, decoder_1_out8, W);
  and and_10 (and_10_out, decoder_1_out9, W);
  and and_11 (and_11_out, decoder_1_out10, W);
  and and_12 (and_12_out, decoder_1_out11, W);
  and and_13 (and_13_out, decoder_1_out12, W);
  and and_14 (and_14_out, decoder_1_out13, W);
  and and_15 (and_15_out, decoder_1_out14, W);
  and and_16 (and_16_out, decoder_1_out15, W);
  and and_17 (and_17_out, decoder_1_out16, W);
  and and_18 (and_18_out, decoder_1_out17, W);
  and and_19 (and_19_out, decoder_1_out18, W);
  and and_20 (and_20_out, decoder_1_out19, W);
  and and_21 (and_21_out, decoder_1_out20, W);
  and and_22 (and_22_out, decoder_1_out21, W);
  and and_23 (and_23_out, decoder_1_out22, W);
  and and_24 (and_24_out, decoder_1_out23, W);
  and and_25 (and_25_out, decoder_1_out24, W);
  and and_26 (and_26_out, decoder_1_out25, W);
  and and_27 (and_27_out, decoder_1_out26, W);
  and and_28 (and_28_out, decoder_1_out27, W);
  and and_29 (and_29_out, decoder_1_out28, W);
  and and_30 (and_30_out, decoder_1_out29, W);
  and and_31 (and_31_out, decoder_1_out30, W);
  and and_32 (and_32_out, decoder_1_out31, W);
  Register #(.width(32)) u_x0 (.D(X0), .en(and_1_out), .Q(x0_q), .clk(clock_1_out));  // open: clr
  Register #(.width(32)) x1 (.D(Data), .en(and_2_out), .Q(x1_q), .clk(clock_1_out));  // open: clr
  Register #(.width(32)) x2 (.D(Data), .en(and_3_out), .Q(x2_q), .clk(clock_1_out));  // open: clr
  Register #(.width(32)) x3 (.D(Data), .en(and_4_out), .Q(x3_q), .clk(clock_1_out));  // open: clr
  Register #(.width(32)) x4 (.D(Data), .en(and_5_out), .Q(x4_q), .clk(clock_1_out));  // open: clr
  Register #(.width(32)) x5 (.D(Data), .en(and_6_out), .Q(x5_q), .clk(clock_1_out));  // open: clr
  Register #(.width(32)) x6 (.D(Data), .en(and_7_out), .Q(x6_q), .clk(clock_1_out));  // open: clr
  Register #(.width(32)) x7 (.D(Data), .en(and_8_out), .Q(x7_q), .clk(clock_1_out));  // open: clr
  Register #(.width(32)) x8 (.D(Data), .en(and_9_out), .Q(x8_q), .clk(clock_1_out));  // open: clr
  Register #(.width(32)) x9 (.D(Data), .en(and_10_out), .Q(x9_q), .clk(clock_1_out));  // open: clr
  Register #(.width(32)) x10 (.D(Data), .en(and_11_out), .Q(x10_q), .clk(clock_1_out));  // open: clr
  Register #(.width(32)) x11 (.D(Data), .en(and_12_out), .Q(x11_q), .clk(clock_1_out));  // open: clr
  Register #(.width(32)) x12 (.D(Data), .en(and_13_out), .Q(x12_q), .clk(clock_1_out));  // open: clr
  Register #(.width(32)) x13 (.D(Data), .en(and_14_out), .Q(x13_q), .clk(clock_1_out));  // open: clr
  Register #(.width(32)) x14 (.D(Data), .en(and_15_out), .Q(x14_q), .clk(clock_1_out));  // open: clr
  Register #(.width(32)) x15 (.D(Data), .en(and_16_out), .Q(x15_q), .clk(clock_1_out));  // open: clr
  Register #(.width(32)) x16 (.D(Data), .en(and_17_out), .Q(x16_q), .clk(clock_1_out));  // open: clr
  Register #(.width(32)) x17 (.D(Data), .en(and_18_out), .Q(x17_q), .clk(clock_1_out));  // open: clr
  Register #(.width(32)) x18 (.D(Data), .en(and_19_out), .Q(x18_q), .clk(clock_1_out));  // open: clr
  Register #(.width(32)) x19 (.D(Data), .en(and_20_out), .Q(x19_q), .clk(clock_1_out));  // open: clr
  Register #(.width(32)) x20 (.D(Data), .en(and_21_out), .Q(x20_q), .clk(clock_1_out));  // open: clr
  Register #(.width(32)) x21 (.D(Data), .en(and_22_out), .Q(x21_q), .clk(clock_1_out));  // open: clr
  Register #(.width(32)) x22 (.D(Data), .en(and_23_out), .Q(x22_q), .clk(clock_1_out));  // open: clr
  Register #(.width(32)) x23 (.D(Data), .en(and_24_out), .Q(x23_q), .clk(clock_1_out));  // open: clr
  Register #(.width(32)) x24 (.D(Data), .en(and_25_out), .Q(x24_q), .clk(clock_1_out));  // open: clr
  Register #(.width(32)) x25 (.D(Data), .en(and_26_out), .Q(x25_q), .clk(clock_1_out));  // open: clr
  Register #(.width(32)) x26 (.D(Data), .en(and_27_out), .Q(x26_q), .clk(clock_1_out));  // open: clr
  Register #(.width(32)) x27 (.D(Data), .en(and_28_out), .Q(x27_q), .clk(clock_1_out));  // open: clr
  Register #(.width(32)) x28 (.D(Data), .en(and_29_out), .Q(x28_q), .clk(clock_1_out));  // open: clr
  Register #(.width(32)) x29 (.D(Data), .en(and_30_out), .Q(x29_q), .clk(clock_1_out));  // open: clr
  Register #(.width(32)) x30 (.D(Data), .en(and_31_out), .Q(x30_q), .clk(clock_1_out));  // open: clr
  Register #(.width(32)) x31 (.D(Data), .en(and_32_out), .Q(x31_q), .clk(clock_1_out));  // open: clr
  Multiplexer #(.select(5), .width(32)) multiplexer_1 (
    .in0(x0_q), .in1(x1_q), .in2(x2_q), .in3(x3_q), .in4(x4_q), .in5(x5_q), .in6(x6_q), .in7(x7_q),
    .in8(x8_q), .in9(x9_q), .in10(x10_q), .in11(x11_q), .in12(x12_q), .in13(x13_q), .in14(x14_q),
    .in15(x15_q), .in16(x16_q), .in17(x17_q), .in18(x18_q), .in19(x19_q), .in20(x20_q), .in21(x21_q),
    .in22(x22_q), .in23(x23_q), .in24(x24_q), .in25(x25_q), .in26(x26_q), .in27(x27_q), .in28(x28_q),
    .in29(x29_q), .in30(x30_q), .in31(x31_q), .out(RA_Output), .sel(RA));  // open: en
  Multiplexer #(.select(5), .width(32)) multiplexer_2 (
    .in0(x0_q), .in1(x1_q), .in2(x2_q), .in3(x3_q), .in4(x4_q), .in5(x5_q), .in6(x6_q), .in7(x7_q),
    .in8(x8_q), .in9(x9_q), .in10(x10_q), .in11(x11_q), .in12(x12_q), .in13(x13_q), .in14(x14_q),
    .in15(x15_q), .in16(x16_q), .in17(x17_q), .in18(x18_q), .in19(x19_q), .in20(x20_q), .in21(x21_q),
    .in22(x22_q), .in23(x23_q), .in24(x24_q), .in25(x25_q), .in26(x26_q), .in27(x27_q), .in28(x28_q),
    .in29(x29_q), .in30(x30_q), .in31(x31_q), .out(RB_Output), .sel(RB));  // open: en
endmodule

module Data_Memory (
  input  [31:0] Address,
  input  [31:0] Data,
  input  Store,
  input  Load,
  input  [2:0] Func3,
  output [31:0] out_6
);

  wire Byte, clock_1_out, comparator_1_eq, comparator_2_eq, comparator_3_eq, comparator_4_eq,
       comparator_6_eq, comparator_7_eq, Half, SByte, SHalf, SWord, Unsigned, W1, W2, W3, W4, Word;
  wire [1:0] priority_encoder_1_out;
  wire [3:0] multiplexer_1_out, multiplexer_7_out, SB_Mask, SH_Mask;
  wire [7:0] LB1, LB2, LB3, LB4, multiplexer_2_out;
  wire [15:0] multiplexer_3_out;
  wire [31:0] bit_extender_1_out, bit_extender_2_out, bit_extender_3_out, bit_extender_4_out,
       multiplexer_5_out, multiplexer_6_out, multiplexer_9_out;

  RAM #(.addrWidth(24), .bus("separate")) ram_1 (
    .addr(Address[23:0]), .din(Data[31:24]), .data(LB4), .str(W4), .clk(clock_1_out), .ld(Load));  // open: sel, clr
  Comparator #(.width(3)) comparator_1 (.a(Func3), .b(3'b000), .eq(comparator_1_eq));  // open: gt, lt
  Comparator #(.width(3)) comparator_2 (.a(Func3), .b(3'b100), .eq(comparator_2_eq));  // open: gt, lt
  Comparator #(.width(3)) comparator_3 (.a(Func3), .b(3'b001), .eq(comparator_3_eq));  // open: gt, lt
  Comparator #(.width(3)) comparator_4 (.a(Func3), .b(3'b101), .eq(comparator_4_eq));  // open: gt, lt
  Comparator #(.width(3)) comparator_5 (.a(Func3), .b(3'b010), .eq(Word));  // open: gt, lt
  Comparator #(.width(3)) comparator_6 (.a(Func3), .b(3'b100), .eq(comparator_6_eq));  // open: gt, lt
  Comparator #(.width(3)) comparator_7 (.a(Func3), .b(3'b101), .eq(comparator_7_eq));  // open: gt, lt
  Comparator #(.width(3)) comparator_8 (.a(Func3), .b(3'b000), .eq(SByte));  // open: gt, lt
  Comparator #(.width(3)) comparator_9 (.a(Func3), .b(3'b001), .eq(SHalf));  // open: gt, lt
  Comparator #(.width(3)) comparator_10 (.a(Func3), .b(3'b010), .eq(SWord));  // open: gt, lt
  or or_1 (Byte, comparator_1_eq, comparator_2_eq);
  or or_2 (Half, comparator_3_eq, comparator_4_eq);
  or or_3 (Unsigned, comparator_6_eq, comparator_7_eq);
  RAM #(.addrWidth(24), .bus("separate")) ram_2 (
    .addr(Address[23:0]), .din(Data[23:16]), .data(LB3), .str(W3), .clk(clock_1_out), .ld(Load));  // open: sel, clr
  Clock clock_1 (.out(clock_1_out));
  Decoder #(.select(2)) decoder_1 (
    .out0(SB_Mask[0]), .out1(SB_Mask[1]), .out2(SB_Mask[2]), .out3(SB_Mask[3]), .sel(Address[1:0]));  // open: en
  Multiplexer #(.width(4)) multiplexer_1 (
    .in0(SB_Mask), .in1(SH_Mask), .out(multiplexer_1_out), .sel(SHalf));  // open: en
  Multiplexer #(.select(2), .width(8)) multiplexer_2 (
    .in0(LB1), .in1(LB2), .in2(LB3), .in3(LB4), .out(multiplexer_2_out), .sel(Address[1:0]));  // open: en
  Multiplexer #(.width(16)) multiplexer_3 (
    .in0({LB2, LB1}), .in1({LB4, LB3}), .out(multiplexer_3_out), .sel(Address[1]));  // open: en
  Multiplexer #(.width(4)) multiplexer_4 (.in0(4'b0011), .in1(4'b1100), .out(SH_Mask), .sel(Address[1]));  // open: en
  assign bit_extender_1_out = {{24{multiplexer_2_out[7]}}, multiplexer_2_out};  // Bit_Extender bit_extender_1
  Multiplexer #(.width(32)) multiplexer_5 (
    .in0(bit_extender_1_out), .in1(bit_extender_2_out), .out(multiplexer_5_out), .sel(Unsigned));  // open: en
  assign bit_extender_2_out = {{24{1'b0}}, multiplexer_2_out};  // Bit_Extender bit_extender_2
  assign bit_extender_3_out = {{16{multiplexer_3_out[15]}}, multiplexer_3_out};  // Bit_Extender bit_extender_3
  Multiplexer #(.width(32)) multiplexer_6 (
    .in0(bit_extender_3_out), .in1(bit_extender_4_out), .out(multiplexer_6_out), .sel(Unsigned));  // open: en
  assign bit_extender_4_out = {{16{1'b0}}, multiplexer_3_out};  // Bit_Extender bit_extender_4
  Multiplexer #(.width(4)) multiplexer_7 (
    .in0(multiplexer_1_out), .in1(4'b1111), .out(multiplexer_7_out), .sel(SWord));  // open: en
  RAM #(.addrWidth(24), .bus("separate")) ram_3 (
    .addr(Address[23:0]), .din(Data[15:8]), .data(LB2), .str(W2), .clk(clock_1_out), .ld(Load));  // open: sel, clr
  Multiplexer #(.width(4)) multiplexer_8 (
    .in0(4'b0000), .in1(multiplexer_7_out), .out({W4, W3, W2, W1}), .sel(Store));  // open: en
  Priority_Encoder #(.select(2)) priority_encoder_1 (
    .in0(Byte), .in1(Half), .in2(Word), .out(priority_encoder_1_out));  // open: in3, gs, en_out, en_in
  RAM #(.addrWidth(24), .bus("separate")) ram_4 (
    .addr(Address[23:0]), .din(Data[7:0]), .data(LB1), .str(W1), .clk(clock_1_out), .ld(Load));  // open: sel, clr
  Multiplexer #(.select(2), .width(32)) multiplexer_9 (
    .in0(multiplexer_5_out), .in1(multiplexer_6_out), .in2({LB4, LB3, LB2, LB1}), .out(multiplexer_9_out),
    .sel(priority_encoder_1_out));  // open: in3, en
  Multiplexer #(.width(32)) multiplexer_10 (
    .in0({32{1'b0}}), .in1(multiplexer_9_out), .out(out_6), .sel(Load));  // open: en

  // Other names for the same wires on the sheet: Address_t[23:0] = Address[23:0]; Offset[1:0] = Address[1:0];
  //   Bit0 = Address[1]; B1[7:0] = Data[7:0]; H1[15:0] = Data[15:0]; B2[7:0] = Data[15:8]; B3[7:0] = Data[23:16];
  //   H2[15:0] = Data[31:16]; B4[7:0] = Data[31:24]; Ld = Load; Str = Store
endmodule

module Main (
);

  wire ALUSrc, and_2_out, B, clock_1_out, J, JSel, Load, main_5_out_4, MemtoReg, or_1_out, Store, Write;
  wire [0:0] and_1_out;
  wire [1:0] ALUOp, ImmSrc;
  wire [2:0] Func3;
  wire [3:0] main_3_alu_signal;
  wire [4:0] Rd, Rs1, Rs2;
  wire [6:0] Func7, Opcode;
  wire [7:0] PC_q_2;
  wire [23:0] PC_q, shifter_1_out;
  wire [31:0] adder_1_out, adder_2_out, adder_3_out, data_memory_1_p6, main_2_out_7, main_4_output,
       multiplexer_1_out, multiplexer_2_out, multiplexer_3_out, multiplexer_4_out, register_file_1_ra_output,
       register_file_1_rb_output;

  Register #(.width(32)) PC (.D(multiplexer_4_out), .Q({PC_q_2, PC_q}), .clk(clock_1_out));  // open: en, clr
  Clock clock_1 (.out(clock_1_out));
  Shifter #(.width(24), .shift("lr")) shifter_1 (.in(PC_q), .\dist (5'b00010), .out(shifter_1_out));
  JALR jalr_1 (.Opcode(Opcode), .out_2(JSel));
  ROM #(.addrWidth(24), .dataWidth(32)) rom_1 (
    .addr(shifter_1_out), .data({Func7, Rs2, Rs1, Func3, Rd, Opcode}));  // open: sel
  main_control_main main_1 (
    .OP_CODE(Opcode), .ImmSRC(ImmSrc), .Jump(J), .ALU_Op(ALUOp), .Branch(B), .MemToReg(MemtoReg),
    .Load(Load), .Store(Store), .AluSRC(ALUSrc), .Write(Write));  // open: Rs2_Used
  immediate_generator_main main_2 (
    .rd(Rd), .rs1(Rs1), .rs2(Rs2), .func7(Func7), .func3(Func3), .opcode(Opcode), .out_7(main_2_out_7));
  Adder #(.width(32)) adder_1 (.a({PC_q_2, PC_q}), .b(32'h4), .out(adder_1_out));  // open: cin, cout
  Register_File register_file_1 (
    .X0({32{1'b0}}), .Data(multiplexer_2_out), .RW(Rd), .W(Write), .RA(Rs1), .RB(Rs2),
    .RA_Output(register_file_1_ra_output), .RB_Output(register_file_1_rb_output));
  Multiplexer #(.width(32)) multiplexer_1 (
    .in0(register_file_1_rb_output), .in1(main_2_out_7), .out(multiplexer_1_out), .sel(ALUSrc));  // open: en
  alu_control_main main_3 (.ALU_Op(ALUOp), .Func3(Func3), .Func7(Func7), .ALU_Signal(main_3_alu_signal));
  alu_main main_4 (
    .OP1(register_file_1_ra_output), .OP2(multiplexer_1_out), .Output(main_4_output), .OP(main_3_alu_signal));
  Multiplexer #(.select(2), .width(32)) multiplexer_2 (
    .in0(main_4_output), .in1(data_memory_1_p6), .in2(adder_1_out), .out(multiplexer_2_out),
    .sel({J, and_1_out[0]}));  // open: in3, en
  and and_1 (and_1_out[0], ~Store, MemtoReg);  // AND_Gate
  Adder #(.width(32)) adder_2 (.a({PC_q_2, PC_q}), .b(main_2_out_7), .out(adder_2_out));  // open: cin, cout
  Adder #(.width(32)) adder_3 (.a(register_file_1_ra_output), .b(main_2_out_7), .out(adder_3_out));  // open: cin, cout
  branch_unit_main main_5 (
    .Data1(register_file_1_ra_output), .Data2(register_file_1_rb_output), .out_4(main_5_out_4), .B_Sel(Func3));
  Multiplexer #(.width(32)) multiplexer_3 (
    .in0(adder_2_out), .in1(adder_3_out), .out(multiplexer_3_out), .sel(JSel));  // open: en
  // Data_Memory data_memory_1: pin names not known; wires that end beside it: main_4_output, register_file_1_rb_output, Load, Func3, Store, data_memory_1_p6
  Multiplexer #(.width(32)) multiplexer_4 (
    .in0(adder_1_out), .in1(multiplexer_3_out), .out(multiplexer_4_out), .sel(or_1_out));  // open: en
  or or_1 (or_1_out, and_2_out, J);
  and and_2 (and_2_out, B, main_5_out_4);

  // Notes on the sheet:
  //   contents of rom_1 (hex, n*v repeats v):
  //   100b7 500113 710193 310233 402182b3 527333 5263b3 524433 42a4b3 40a023 a503 a20463 100593 80066f
  //   100693 60067
endmodule

module JALR (
  input  [6:0] Opcode,
  output out_2
);

  Comparator #(.width(7)) comparator_1 (.a(Opcode), .b(7'b1100111), .eq(out_2));  // open: gt, lt
endmodule
